# Fritzing sketch parts (saved by Fritzing 0.9.3b)
breadboards: 1

parts:
  U2 = NodeMCU V1.0
  OLED1 = OLED 128x64 I2C Monochrome Display
  220V_AC_Relay = RELAY-SOLIDSTATE [package=relay-s108t02]
  Relay = Keyes Relay [package=THT]
  7_-_9V_1a = Power plug
  HID_Card_Reader = Header 4 [package=1x04-1mm-ra]

nets:
  N1: U2.D1, OLED1.SCK
  N2: U2.D2, OLED1.SDA
  3V3: U2.3V3, OLED1.VDD, Relay.signal
  GND: U2.GND, OLED1.GND, 220V_AC_Relay.-, Relay.ground, 7_-_9V_1a.GND, HID_Card_Reader.3
  N3: U2.D5, HID_Card_Reader.2
  N4: U2.D6, HID_Card_Reader.1
  N5: U2.D8, U2.SD3, Relay.power
  VIN: U2.Vin, Relay.C, 7_-_9V_1a.VCC, HID_Card_Reader.4
  N6: 220V_AC_Relay.+, Relay.NO

custom parts:
  NodeMCU V1.0: ESP8266 based NodeMCU
  Keyes Relay: The Keyes 5V relay module is suitable for SCM development, home appliance control. It uses a 5V~12V TIL control signal which can control DC / AC signal.
